# Fritzing sketch v0.1 (saved by Fritzing 0.9.3b)
breadboards: 1

parts:
  Part1 = LightBlue Bean
  S5 = Momentary Switch [package=ksa_sealed_tac_switch]
  S4 = Momentary Switch [package=ksa_sealed_tac_switch]
  S3 = Momentary Switch [package=ksa_sealed_tac_switch]
  S2 = Momentary Switch [package=ksa_sealed_tac_switch]
  S1 = Momentary Switch [package=ksa_sealed_tac_switch]
  S6 = Momentary Switch [package=ksa_sealed_tac_switch]

nets:
  N1: Part1.D5/SCK, S6.1
  N2: Part1.D4/MISO, S5.1
  N3: Part1.D3/MOSI, S4.1
  N4: Part1.D2, S3.1
  N5: Part1.D1, S2.1
  N6: Part1.D0, S1.1
  N7: Part1.GND, S5.4, S4.4, S3.4, S2.4, S1.4, S6.4
